# Fritzing sketch LED-Many (saved by Fritzing 0.9.3b)

parts:
  LED1 = LEDs [package=fkit-led-1206]
  LED2 = LEDs [package=fkit-led-1206]
  Z1 = VARISTOR [package=0402-res]
  Z2 = VARISTOR [package=0402-res]
  BAT1 = Battery Holders [package=battcon_245mm_pth]
  LED3 = LEDs [package=fkit-led-1206]
  LED4 = LEDs [package=fkit-led-1206]
  LED5 = LEDs [package=fkit-led-1206]
  LED6 = LEDs [package=fkit-led-1206]

nets:
  N1: LED1.A, Z1.1
  N2: LED1.C, LED3.A
  N3: LED2.A, LED5.C
  N4: LED2.C, LED6.A
  N5: Z1.2, Z2.2, BAT1.+
  N6: Z2.1, LED5.A
  N7: BAT1.-, LED4.C, LED6.C
  N8: LED3.C, LED4.A
