# Fritzing sketch LED-TEST-Fzz (saved by Fritzing 0.9.3b)

parts:
  R1 = Resistor [tolerance=±5% resistance=220 package=THT]
  R2 = Resistor [tolerance=±5% resistance=220 package=THT]
  LED1 = LED - 5mm [color="Red (633nm)" package="5 mm [THT]"]
  LED2 = LED - 5mm [color="Red (633nm)" package="5 mm [THT]"]
  BAT1 = Battery Holders [package=battcon_245mm_pth]

nets:
  N1: R1.Pin_0, LED1.anode
  N2: R1.Pin_1, R2.Pin_1, BAT1.+
  N3: R2.Pin_0, LED2.anode
  N4: LED1.cathode, LED2.cathode, BAT1.-
